# Fritzing sketch Rover (saved by Fritzing 1.0.6)
breadboards: 1

parts:
  A1 = Sabertooth2x12
  A2 = Sabertooth2x12
  DX_P = DC Motor with two-phase hall-encoder [part_number=VT-E-G25A-06-177E]
  SX_A = DC Motor with two-phase hall-encoder [part_number=VT-E-G25A-06-177E]
  SX_P = DC Motor with two-phase hall-encoder [part_number=VT-E-G25A-06-177E]
  J1 = STM32 Nucleo boards
  J2 = STM32 Nucleo boards
  Componente1 = InvenSense MPU6050
  5V = Camdenboss CTB0158-5 [part_number=CTB0158-5 package=THT]
  12V = Camdenboss CTB0158-5 [part_number=CTB0158-5 package=THT]
  5V1 = Camdenboss CTB0158-5 [part_number=CTB0158-5 package=THT]
  UART_5 = Camdenboss CTB0158-3 [part_number=CTB0158-3 package=THT]
  U2 = ESP32-38PinWide [part_number=ESP32-38PinWide]
  SONAR_SX = HC-SR04 [chip_label=IC package="SIP (Single Inline) [THT]"]
  SONAR_DX = HC-SR04 [chip_label=IC package="SIP (Single Inline) [THT]"]
  SONAR_F = HC-SR04 [chip_label=IC package="SIP (Single Inline) [THT]"]
  5V3 = Camdenboss CTB0158-5 [part_number=CTB0158-5 package=THT]
  SONAR_TRIG = Camdenboss CTB0158-4 [part_number=CTB0158-4 package=THT]
  M1 = RioRand LM2596
  U1 = LIPO-2000mAh [package=lipo-2000]
  DX_A = DC Motor with two-phase hall-encoder [part_number=VT-E-G25A-06-177E]
  U3 = LIPO-2000mAh [package=lipo-2000]
  U4 = LIPO-2000mAh [package=lipo-2000]
  5V4 = Camdenboss CTB0158-5 [part_number=CTB0158-5 package=THT]
  LED_LEFT = LED - 5mm [color="Yellow (595nm)" current=0.030A package="5 mm [THT]"]
  LED_RIGHT = LED - 5mm [color="Yellow (595nm)" current=0.030A package="5 mm [THT]"]
  LED_BLU = LED - 5mm [color="Blue (430nm)" current=0.030A package="5 mm [THT]"]
  LED_RED = LED - 5mm [color="Red (635nm)" current=0.030A package="5 mm [THT]"]
  R6 = Resistor [tolerance=±5% power=0.25W resistance=220 package=THT]
  R7 = Resistor [tolerance=±5% power=0.25W resistance=220 package=THT]
  R8 = Resistor [tolerance=±5% power=0.25W resistance=220 package=THT]
  R9 = Resistor [tolerance=±5% power=0.25W resistance=220 package=THT]
  R10 = Resistor [tolerance=±5% power=0.25W resistance=10k package=THT]
  R11 = Resistor [tolerance=±5% power=0.25W resistance=4.7k package=THT]
  R12 = Resistor [tolerance=±5% power=0.25W resistance=4.7k package=THT]
  UART_6 = Camdenboss CTB0158-3 [part_number=CTB0158-3 package=THT]
  GROUND = Camdenboss CTB0158-8 [part_number=CTB0158-8 package=THT]
  GROUND_3 = Camdenboss CTB0158-7 [part_number=CTB0158-7 package=THT]
  IC1 = DIP - 6 pins [chip_label="5V RELAY" package="DIP (Dual Inline) [THT]"]
  IC2 = DIP - 6 pins [chip_label="5V RELAY" package="DIP (Dual Inline) [THT]"]
  5V5 = Camdenboss CTB0158-3 [part_number=CTB0158-3 package=THT]
  GROUND_2 = Camdenboss CTB0158-8 [part_number=CTB0158-8 package=THT]
  UART_7 = Camdenboss CTB0158-3 [part_number=CTB0158-3 package=THT]
  UART_8 = Camdenboss CTB0158-3 [part_number=CTB0158-3 package=THT]

nets:
  N1: A1.Pin_1, GROUND.terminal_4
  N2: A1.Pin_3, UART_5.terminal_3
  N3: A1.Pin_4, UART_6.terminal_1
  N4: A1.Pin_5, SX_A.pin1
  N5: A1.Pin_6, SX_A.pin2
  N6: A1.Pin_7, 12V.terminal_4
  N7: A1.Pin_8, GROUND.terminal_3
  N8: A1.Pin_9, DX_A.pin1
  N9: A1.Pin_10, DX_A.pin2
  N10: A2.Pin_1, GROUND_2.terminal_2
  N11: A2.Pin_3, UART_5.terminal_1
  N12: A2.Pin_4, UART_6.terminal_3
  N13: A2.Pin_5, DX_P.pin1
  N14: A2.Pin_6, DX_P.pin2
  N15: A2.Pin_7, 12V.terminal_5
  N16: A2.Pin_8, GROUND.terminal_5
  N17: A2.Pin_9, SX_P.pin1
  N18: A2.Pin_10, SX_P.pin2
  N19: DX_P.pin3, GROUND_2.terminal_5
  N20: DX_P.pin4, 5V.terminal_5
  N21: DX_P.pin5, J1.PA4
  N22: DX_P.pin6, J1.PB4
  N23: SX_A.pin3, GROUND.terminal_2
  N24: SX_A.pin4, 5V4.terminal_5
  N25: SX_A.pin5, J1.PA15
  N26: SX_A.pin6, J1.PA1
  N27: SX_P.pin3, GROUND_2.terminal_1
  N28: SX_P.pin4, 5V.terminal_1
  N29: SX_P.pin5, J1.PC0
  N30: SX_P.pin6, J1.PC1
  N31: J1.PC8, LED_BLU.anode
  N32: J1.PC6, LED_LEFT.anode
  N33: J1.PA12, DX_A.pin5
  N34: J1.PA11, DX_A.pin6
  N35: J1.PC11, J2.PC10
  N36: J1.PD2, IC1.NO
  N37: J1.GND, GROUND_2.terminal_3
  N38: J1.5V, 5V.terminal_3
  N39: J1.PC9, LED_RIGHT.anode
  N40: J1.PB8, LED_RED.anode
  N41: J1.PA0, R11.Pin_0, R12.Pin_1
  N42: J1.PC10, J2.PC11
  N43: J1.PC12, IC2.NO
  N44: J1.PB7, UART_8.terminal_3
  N45: J2.A0, SONAR_TRIG.terminal_1
  N46: J2.PC8, Componente1.SCL
  N47: J2.PD2, IC1.NC
  N48: J2.A4/SDA, U2.GPIO21
  N49: J2.A5/SCL, U2.GPIO22
  N50: J2.5V, 5V1.terminal_4
  N51: J2.GND, GROUND_3.terminal_1
  N52: J2.PC9, Componente1.SDA
  N53: J2.PC1, SONAR_SX.Echo
  N54: J2.PC0, SONAR_F.Echo
  N55: J2.PC12, IC2.NC
  N56: J2.PC2, SONAR_DX.Echo
  N57: Componente1.VCC, 5V1.terminal_5
  N58: Componente1.GND, GROUND_3.terminal_5
  N59: 5V.terminal_2, 5V4.terminal_2
  N60: 5V.terminal_4, DX_A.pin4
  N61: 12V.terminal_1, U4.+
  N62: 12V.terminal_2, M1.Pin_1
  N63: 12V.terminal_3, R10.Pin_1
  N64: 5V1.terminal_1, 5V4.terminal_3
  N65: 5V1.terminal_2, U2.VIN
  N66: 5V1.terminal_3, 5V3.terminal_4
  N67: UART_5.terminal_2, IC2.CO
  N68: U2.GPIO11, GROUND_3.terminal_7
  N69: SONAR_SX.Vcc, 5V3.terminal_1
  N70: SONAR_SX.Trig, SONAR_TRIG.terminal_2
  N71: SONAR_SX.GND, GROUND_3.terminal_2
  N72: SONAR_DX.Vcc, 5V3.terminal_3
  N73: SONAR_DX.Trig, SONAR_TRIG.terminal_4
  N74: SONAR_DX.GND, GROUND_3.terminal_4
  N75: SONAR_F.Vcc, 5V3.terminal_2
  N76: SONAR_F.Trig, SONAR_TRIG.terminal_3
  N77: SONAR_F.GND, GROUND_3.terminal_3
  N78: 5V3.terminal_5, 5V5.terminal_2
  N79: M1.Pin_2, U1.-
  N80: M1.Pin_3, 5V4.terminal_1
  N81: M1.Pin_4, GROUND.terminal_1
  N82: U1.+, U3.-
  N83: DX_A.pin3, GROUND_2.terminal_4
  N84: U3.+, U4.-
  N85: LED_LEFT.cathode, R9.Pin_1
  N86: LED_RIGHT.cathode, R8.Pin_1
  N87: LED_BLU.cathode, R6.Pin_1
  N88: LED_RED.cathode, R7.Pin_1
  N89: R6.Pin_0, R7.Pin_0, R12.Pin_0, GROUND.terminal_7
  N90: R8.Pin_0, R9.Pin_0, GROUND.terminal_6
  N91: R10.Pin_0, R11.Pin_1
  N92: UART_6.terminal_2, IC1.CO
  N93: GROUND.terminal_8, GROUND_2.terminal_6
  N94: GROUND_3.terminal_6, GROUND_2.terminal_7
  N95: IC1.DC+, 5V5.terminal_1
  N96: IC1.DC-, UART_7.terminal_2
  N97: IC1.IN, UART_8.terminal_2
  N98: IC2.DC+, 5V5.terminal_3
  N99: IC2.DC-, UART_7.terminal_1
  N100: IC2.IN, UART_8.terminal_1
  N101: GROUND_2.terminal_8, UART_7.terminal_3

custom parts:
  Sabertooth2x12: The Sabertooth 2X12 is one of the most versatile, efficient and easy to use dual motor drivers on the market.
  ESP32-38PinWide: Generic 38-Pin ESP32 with wide format (only access to one side of pins on a breadboard) based on Stephen Lilley's HiLetgo ESP-WROOM-32 ESP32 ESP-32S Development Board.
  HC-SR04: HC-SR04 ultrasound distance sensor
  DIP - 6 pins: A DIP stand-in part for whatever IC you want. With 6 pins on a 300mil dual inline package (DIP) footprint.
